// Logisim project CPU.circ as structural Verilog: 1 circuit, main circuit main
module main (
  input  in_1
);

  wire clock_1_out, clock_2_out;
  wire [6:0] keyboard_1_data;
  wire [7:0] counter_1_q, rom_1_data;

  Clock clock_1 (.out(clock_1_out));
  Clock clock_2 (.out(clock_2_out));
  Counter #(.max('h35)) counter_1 (.Q(counter_1_q), .clk(clock_1_out), .clr(in_1));  // open: load, D, count, carry
  Keyboard keyboard_1 (.clk(clock_2_out), .re(1'b1), .data(keyboard_1_data));  // open: clr, avail
  ROM rom_1 (.addr(counter_1_q), .data(rom_1_data), .sel(1'b1));
  TTY tty_1 (.data(keyboard_1_data), .clk(clock_2_out), .we(1'b1));  // open: clr
  TTY tty_2 (.data(rom_1_data[6:0]), .clk(clock_1_out), .we(1'b1));  // open: clr

  // Notes on the sheet:
  //   contents of rom_1 (hex, n*v repeats v):
  //   4d 61 72 61 20 64 61 6a 20 64 6f 6e 65 73 69 20 64 65 63 6b 69 6d 61 20 6a 6f 73 20 6a 65 64 6e 75
  //   20 72 75 6e 64 75 20 6b 61 72 6c 6f 76 61 63 6b 6f 67 a a
endmodule
