// Logisim project CPU_design.circ as structural Verilog: 1 circuit, main circuit main
module main (
);

  wire and_1_out, and_2_out, and_3_out, and_4_out, and_5_out, and_6_out, and_7_out, and_8_out, and_9_out,
       and_10_out, and_11_out, and_12_out, and_13_out, and_14_out, and_15_out, clock_1_out, d_ff_1_q,
       keyboard_1_avail, nand_1_out, nand_2_out, nand_3_out, nand_4_out, nand_5_out, nand_6_out, nand_7_out,
       nand_8_out, nor_1_out, not_1_out, not_2_out, not_3_out, not_4_out, not_5_out, not_6_out, not_7_out,
       or_1_out, or_2_out, or_3_out, or_4_out, or_5_out, or_6_out, or_7_out, or_8_out, or_9_out, or_10_out,
       or_11_out, or_12_out, or_13_out, or_14_out, or_15_out, or_16_out, or_17_out, xor_1_out, xor_2_out,
       xor_3_out, xor_4_out, xor_5_out, xor_6_out, xor_7_out, xor_8_out;
  wire [2:0] keyboard_1_data_2;
  wire [3:0] keyboard_1_data;
  wire [7:0] controlled_buffer_1_out, controlled_buffer_25_out, counter_1_q, ram_1_data, register_1_q,
       register_2_q, register_3_q;
  wire [11:0] rom_1_data;

  not not_1 (not_1_out, or_1_out);
  Counter counter_1 (
    .load(or_1_out), .D(controlled_buffer_1_out), .count(not_1_out), .Q(counter_1_q), .clk(clock_1_out));  // open: carry, clr
  ROM #(.dataWidth(12)) rom_1 (.addr(counter_1_q), .data(rom_1_data), .sel(1'b1));
  not not_2 (not_2_out, rom_1_data[11]);
  assign controlled_buffer_1_out[0] = or_2_out ? rom_1_data[0] : 1'bz;  // Controlled_Buffer controlled_buffer_1
  not not_3 (not_3_out, rom_1_data[8]);
  not not_4 (not_4_out, rom_1_data[10]);
  not not_5 (not_5_out, rom_1_data[9]);
  assign controlled_buffer_1_out[1] = or_2_out ? rom_1_data[1] : 1'bz;  // Controlled_Buffer controlled_buffer_2
  assign controlled_buffer_1_out[2] = or_2_out ? rom_1_data[2] : 1'bz;  // Controlled_Buffer controlled_buffer_3
  assign controlled_buffer_1_out[3] = or_2_out ? rom_1_data[3] : 1'bz;  // Controlled_Buffer controlled_buffer_4
  assign controlled_buffer_1_out[4] = or_2_out ? rom_1_data[4] : 1'bz;  // Controlled_Buffer controlled_buffer_5
  and and_1 (and_1_out, not_3_out, not_5_out, not_4_out, not_2_out);
  and and_2 (and_2_out, rom_1_data[8], not_5_out, not_4_out, not_2_out);
  and and_3 (and_3_out, not_3_out, rom_1_data[9], not_4_out, not_2_out);
  and and_4 (and_4_out, rom_1_data[8], rom_1_data[9], not_4_out, not_2_out);
  and and_5 (and_5_out, not_3_out, not_5_out, rom_1_data[10], not_2_out);
  and and_6 (and_6_out, rom_1_data[8], not_5_out, rom_1_data[10], not_2_out);
  and and_7 (and_7_out, not_3_out, rom_1_data[9], rom_1_data[10], not_2_out);
  and and_8 (and_8_out, rom_1_data[8], rom_1_data[9], rom_1_data[10], not_2_out);
  and and_9 (and_9_out, not_3_out, not_5_out, not_4_out, rom_1_data[11]);
  and and_10 (and_10_out, rom_1_data[8], not_5_out, not_4_out, rom_1_data[11]);
  and and_11 (and_11_out, not_3_out, rom_1_data[9], not_4_out, rom_1_data[11]);
  and and_12 (and_12_out, rom_1_data[8], rom_1_data[9], not_4_out, rom_1_data[11]);
  and and_13 (and_13_out, not_3_out, not_5_out, rom_1_data[10], rom_1_data[11]);
  Clock clock_1 (.out(clock_1_out));
  assign controlled_buffer_1_out[5] = or_2_out ? rom_1_data[5] : 1'bz;  // Controlled_Buffer controlled_buffer_6
  assign controlled_buffer_1_out[6] = or_2_out ? rom_1_data[6] : 1'bz;  // Controlled_Buffer controlled_buffer_7
  assign controlled_buffer_1_out[7] = or_2_out ? rom_1_data[7] : 1'bz;  // Controlled_Buffer controlled_buffer_8
  or or_1 (or_1_out, and_11_out, and_14_out, and_15_out);
  and and_14 (and_14_out, and_12_out, d_ff_1_q);
  and and_15 (and_15_out, not_6_out, and_13_out);
  not not_6 (not_6_out, d_ff_1_q);
  not not_7 (not_7_out, or_5_out);
  RAM ram_1 (.addr(rom_1_data[7:0]), .data(ram_1_data), .sel(1'b1), .clk(clock_1_out), .ld(not_7_out));  // open: clr
  or or_2 (or_2_out, or_3_out, or_4_out);
  or or_3 (or_3_out, and_1_out, and_2_out, and_8_out);
  or or_4 (or_4_out, and_10_out, and_11_out, and_12_out, and_13_out);
  assign ram_1_data[0] = or_5_out ? controlled_buffer_1_out[0] : 1'bz;  // Controlled_Buffer controlled_buffer_9
  assign ram_1_data[1] = or_5_out ? controlled_buffer_1_out[1] : 1'bz;  // Controlled_Buffer controlled_buffer_10
  assign ram_1_data[2] = or_5_out ? controlled_buffer_1_out[2] : 1'bz;  // Controlled_Buffer controlled_buffer_11
  assign ram_1_data[3] = or_5_out ? controlled_buffer_1_out[3] : 1'bz;  // Controlled_Buffer controlled_buffer_12
  assign controlled_buffer_1_out[0] = or_6_out ? ram_1_data[0] : 1'bz;  // Controlled_Buffer controlled_buffer_13
  assign controlled_buffer_1_out[1] = or_6_out ? ram_1_data[1] : 1'bz;  // Controlled_Buffer controlled_buffer_14
  buf or_5 (or_5_out, and_6_out);  // OR_Gate
  assign ram_1_data[4] = or_5_out ? controlled_buffer_1_out[4] : 1'bz;  // Controlled_Buffer controlled_buffer_15
  assign ram_1_data[5] = or_5_out ? controlled_buffer_1_out[5] : 1'bz;  // Controlled_Buffer controlled_buffer_16
  assign ram_1_data[6] = or_5_out ? controlled_buffer_1_out[6] : 1'bz;  // Controlled_Buffer controlled_buffer_17
  assign ram_1_data[7] = or_5_out ? controlled_buffer_1_out[7] : 1'bz;  // Controlled_Buffer controlled_buffer_18
  assign controlled_buffer_1_out[2] = or_6_out ? ram_1_data[2] : 1'bz;  // Controlled_Buffer controlled_buffer_19
  assign controlled_buffer_1_out[3] = or_6_out ? ram_1_data[3] : 1'bz;  // Controlled_Buffer controlled_buffer_20
  assign controlled_buffer_1_out[4] = or_6_out ? ram_1_data[4] : 1'bz;  // Controlled_Buffer controlled_buffer_21
  assign controlled_buffer_1_out[5] = or_6_out ? ram_1_data[5] : 1'bz;  // Controlled_Buffer controlled_buffer_22
  or or_6 (or_6_out, and_5_out, and_9_out);
  assign controlled_buffer_1_out[6] = or_6_out ? ram_1_data[6] : 1'bz;  // Controlled_Buffer controlled_buffer_23
  assign controlled_buffer_1_out[7] = or_6_out ? ram_1_data[7] : 1'bz;  // Controlled_Buffer controlled_buffer_24
  buf or_7 (or_7_out, and_9_out);  // OR_Gate
  or or_8 (or_8_out, and_3_out, and_4_out, and_5_out, and_8_out);
  assign controlled_buffer_25_out[0] = or_8_out ? controlled_buffer_1_out[0] : 1'bz;  // Controlled_Buffer controlled_buffer_25
  assign controlled_buffer_25_out[1] = or_8_out ? controlled_buffer_1_out[1] : 1'bz;  // Controlled_Buffer controlled_buffer_26
  assign controlled_buffer_25_out[2] = or_8_out ? controlled_buffer_1_out[2] : 1'bz;  // Controlled_Buffer controlled_buffer_27
  assign controlled_buffer_25_out[2] = or_7_out ? nand_6_out : 1'bz;  // Controlled_Buffer controlled_buffer_28
  assign controlled_buffer_25_out[1] = or_7_out ? nand_7_out : 1'bz;  // Controlled_Buffer controlled_buffer_29
  assign controlled_buffer_25_out[0] = or_7_out ? nand_8_out : 1'bz;  // Controlled_Buffer controlled_buffer_30
  assign controlled_buffer_25_out[3] = or_8_out ? controlled_buffer_1_out[3] : 1'bz;  // Controlled_Buffer controlled_buffer_31
  assign controlled_buffer_25_out[4] = or_8_out ? controlled_buffer_1_out[4] : 1'bz;  // Controlled_Buffer controlled_buffer_32
  assign controlled_buffer_25_out[5] = or_8_out ? controlled_buffer_1_out[5] : 1'bz;  // Controlled_Buffer controlled_buffer_33
  assign controlled_buffer_25_out[6] = or_8_out ? controlled_buffer_1_out[6] : 1'bz;  // Controlled_Buffer controlled_buffer_34
  assign controlled_buffer_25_out[6] = or_7_out ? nand_2_out : 1'bz;  // Controlled_Buffer controlled_buffer_35
  assign controlled_buffer_25_out[5] = or_7_out ? nand_3_out : 1'bz;  // Controlled_Buffer controlled_buffer_36
  assign controlled_buffer_25_out[4] = or_7_out ? nand_4_out : 1'bz;  // Controlled_Buffer controlled_buffer_37
  assign controlled_buffer_25_out[3] = or_7_out ? nand_5_out : 1'bz;  // Controlled_Buffer controlled_buffer_38
  assign controlled_buffer_25_out[7] = or_8_out ? controlled_buffer_1_out[7] : 1'bz;  // Controlled_Buffer controlled_buffer_39
  assign controlled_buffer_25_out[7] = or_7_out ? nand_1_out : 1'bz;  // Controlled_Buffer controlled_buffer_40
  or or_9 (or_9_out, or_10_out, or_11_out);
  or or_10 (or_10_out, and_3_out, and_4_out, and_5_out);
  Register register_1 (.D(controlled_buffer_25_out), .en(or_9_out), .Q(register_1_q), .clk(clock_1_out));  // open: clr
  nand nand_1 (nand_1_out, register_1_q[7], controlled_buffer_1_out[7]);
  nand nand_2 (nand_2_out, register_1_q[6], controlled_buffer_1_out[6]);
  nand nand_3 (nand_3_out, register_1_q[5], controlled_buffer_1_out[5]);
  nand nand_4 (nand_4_out, register_1_q[4], controlled_buffer_1_out[4]);
  nand nand_5 (nand_5_out, register_1_q[3], controlled_buffer_1_out[3]);
  nand nand_6 (nand_6_out, register_1_q[2], controlled_buffer_1_out[2]);
  nand nand_7 (nand_7_out, register_1_q[1], controlled_buffer_1_out[1]);
  nand nand_8 (nand_8_out, register_1_q[0], controlled_buffer_1_out[0]);
  or or_11 (or_11_out, and_8_out, and_9_out);
  assign controlled_buffer_1_out[0] = or_13_out ? register_1_q[0] : 1'bz;  // Controlled_Buffer controlled_buffer_41
  assign controlled_buffer_1_out[1] = or_13_out ? register_1_q[1] : 1'bz;  // Controlled_Buffer controlled_buffer_42
  assign controlled_buffer_1_out[2] = or_13_out ? register_1_q[2] : 1'bz;  // Controlled_Buffer controlled_buffer_43
  xor xor_1 (xor_1_out, register_1_q[7], controlled_buffer_1_out[7]);
  xor xor_2 (xor_2_out, register_1_q[6], controlled_buffer_1_out[6]);
  xor xor_3 (xor_3_out, register_1_q[5], controlled_buffer_1_out[5]);
  xor xor_4 (xor_4_out, register_1_q[4], controlled_buffer_1_out[4]);
  xor xor_5 (xor_5_out, register_1_q[3], controlled_buffer_1_out[3]);
  xor xor_6 (xor_6_out, register_1_q[2], controlled_buffer_1_out[2]);
  xor xor_7 (xor_7_out, register_1_q[1], controlled_buffer_1_out[1]);
  xor xor_8 (xor_8_out, register_1_q[0], controlled_buffer_1_out[0]);
  nor nor_1 (nor_1_out, xor_8_out, xor_7_out, xor_6_out, xor_5_out, xor_4_out, xor_3_out, xor_2_out, xor_1_out);
  assign controlled_buffer_1_out[3] = or_13_out ? register_1_q[3] : 1'bz;  // Controlled_Buffer controlled_buffer_44
  assign controlled_buffer_1_out[4] = or_13_out ? register_1_q[4] : 1'bz;  // Controlled_Buffer controlled_buffer_45
  assign controlled_buffer_1_out[5] = or_13_out ? register_1_q[5] : 1'bz;  // Controlled_Buffer controlled_buffer_46
  assign controlled_buffer_1_out[6] = or_13_out ? register_1_q[6] : 1'bz;  // Controlled_Buffer controlled_buffer_47
  D_Flip_Flop d_ff_1 (.clk(clock_1_out), .D(nor_1_out), .Q(d_ff_1_q), .en(or_12_out));  // open: Qn, preset, reset
  buf or_12 (or_12_out, and_10_out);  // OR_Gate
  assign controlled_buffer_1_out[7] = or_13_out ? register_1_q[7] : 1'bz;  // Controlled_Buffer controlled_buffer_48
  or or_13 (or_13_out, and_6_out, and_7_out);
  Hex_Digit_Display hex_digit_display_1 (.value(controlled_buffer_1_out[7:4]));  // open: dp
  Hex_Digit_Display hex_digit_display_2 (.value(controlled_buffer_1_out[3:0]));  // open: dp
  or or_14 (or_14_out, and_1_out, and_7_out);
  Register register_2 (.D(controlled_buffer_1_out), .en(or_14_out), .Q(register_2_q), .clk(clock_1_out));  // open: clr
  buf or_15 (or_15_out, and_2_out);  // OR_Gate
  Register register_3 (.D(controlled_buffer_1_out), .en(or_15_out), .Q(register_3_q), .clk(clock_1_out));  // open: clr
  assign controlled_buffer_1_out[0] = or_16_out ? keyboard_1_avail : 1'bz;  // Controlled_Buffer controlled_buffer_49
  assign controlled_buffer_1_out[1] = or_16_out ? 1'b0 : 1'bz;  // Controlled_Buffer controlled_buffer_50
  assign controlled_buffer_1_out[2] = or_16_out ? 1'b0 : 1'bz;  // Controlled_Buffer controlled_buffer_51
  assign controlled_buffer_1_out[0] = or_17_out ? keyboard_1_data[0] : 1'bz;  // Controlled_Buffer controlled_buffer_52
  buf or_16 (or_16_out, and_3_out);  // OR_Gate
  assign controlled_buffer_1_out[3] = or_16_out ? 1'b0 : 1'bz;  // Controlled_Buffer controlled_buffer_53
  assign controlled_buffer_1_out[4] = or_16_out ? 1'b0 : 1'bz;  // Controlled_Buffer controlled_buffer_54
  assign controlled_buffer_1_out[5] = or_16_out ? 1'b0 : 1'bz;  // Controlled_Buffer controlled_buffer_55
  assign controlled_buffer_1_out[6] = or_16_out ? 1'b0 : 1'bz;  // Controlled_Buffer controlled_buffer_56
  assign controlled_buffer_1_out[1] = or_17_out ? keyboard_1_data[1] : 1'bz;  // Controlled_Buffer controlled_buffer_57
  assign controlled_buffer_1_out[2] = or_17_out ? keyboard_1_data[2] : 1'bz;  // Controlled_Buffer controlled_buffer_58
  assign controlled_buffer_1_out[3] = or_17_out ? keyboard_1_data[3] : 1'bz;  // Controlled_Buffer controlled_buffer_59
  assign controlled_buffer_1_out[4] = or_17_out ? keyboard_1_data_2[0] : 1'bz;  // Controlled_Buffer controlled_buffer_60
  buf or_17 (or_17_out, and_4_out);  // OR_Gate
  assign controlled_buffer_1_out[7] = or_16_out ? 1'b0 : 1'bz;  // Controlled_Buffer controlled_buffer_61
  assign controlled_buffer_1_out[5] = or_17_out ? keyboard_1_data_2[1] : 1'bz;  // Controlled_Buffer controlled_buffer_62
  assign controlled_buffer_1_out[6] = or_17_out ? keyboard_1_data_2[2] : 1'bz;  // Controlled_Buffer controlled_buffer_63
  assign controlled_buffer_1_out[7] = or_17_out ? 1'b0 : 1'bz;  // Controlled_Buffer controlled_buffer_64
  TTY #(.rows(16)) tty_1 (.data(register_2_q[6:0]), .clk(clock_1_out), .we(register_3_q[0]));  // open: clr
  Keyboard keyboard_1 (
    .clk(clock_1_out), .re(register_3_q[1]), .avail(keyboard_1_avail),
    .data({keyboard_1_data_2, keyboard_1_data}));  // open: clr
  Hex_Digit_Display hex_digit_display_3 (.value({1'b0, keyboard_1_data_2}));  // open: dp
  Hex_Digit_Display hex_digit_display_4 (.value(keyboard_1_data));  // open: dp

  // Notes on the sheet:
  //   IP
  //   Program memory
  //   contents of rom_1 (hex, n*v repeats v):
  //   101 57 65 6c 63 6f 6d 65 20 74 6f 20 74 68 65 20 55 73 65 6c 65 73 73 0 4f 53 20 76 37 2e 33 a 42 79
  //   20 44 61 6e 69 6a 65 6c 20 4b 6f 72 65 6e 74 a 100 700 500 0 101 a a 53 68 65 6c 6c 3a 3e 20 0 100
  //   200 901 c43 300 102 100 600 101 100 501 400 900 c52 401 500 401 90a c43 400 90a b33 968 b7f 0 101 a
  //   49 27 6d 20 61 66 72 61 69 64 20 49 20 63 61 6e 27 74 20 64 6f 20 74 68 61 74 2c 20 44 61 76 65 100
  //   a33 0 101 a 41 76 61 69 6c 61 62 6c 65 20 63 6f 6d 6d 61 6e 64 73 3a a a 20 20 20 68 65 6c 70 20 2d
  //   20 70 72 69 6e 74 73 20 74 68 69 73 20 6d 65 73 73 61 67 65 100 a33 a33 20 20 68 65 6c 70 20 2d 20
  //   70 72 69 6e 74 73 20 74 68 69 73 20 6d 65 73 73 61 67 65 100 a33
  //   BUS to IP
  //   RAM
  //   Equal FLAG
  //   Reg A
  //   Equal Flag
  //   8bit DATA BUS
  //   Set IO1 TTY
  //   Reg OUT1
  //   Reg OUT2
  //   IN1
  //   KEYB to BUS
  //   (0xx) Mov OUT1, imm
  //   (1xx) Mov OUT2, imm
  //   (2xx) Mov A, IN1
  //   (3xx) Mov A, IN2
  //   (4xx) Mov A, RAM
  //   (5xx) Mov RAM, A
  //   (6xx) Mov OUT1, A
  //   (7xx) Mov A, imm
  //   (8xx) Nand A, RAM
  //   (9xx) Cmp A, imm
  //   (Axx) Jmp addr
  //   (Bxx) Je addr - jump if equal flag = 1
  //   (Cxx) Jne addr - jump if equal flag = 0
  //   IN2
  //   TTY
  //   Keyboard input
endmodule
